// Logisim project SPM.circ as structural Verilog: 8 circuits, main circuit main
module CSADD (
  input  X,
  input  Y,
  input  in_3,
  input  rst,
  output SUM
);

  wire and_1_out, d_ff_2_q, ha_1_out_3, ha_1_out_4, xor_1_out, xor_2_out;

  HA ha_1 (.in_1(Y), .in_2(d_ff_2_q), .out_3(ha_1_out_3), .out_4(ha_1_out_4));
  and and_1 (and_1_out, X, ha_1_out_3);
  xor xor_1 (xor_1_out, X, ha_1_out_3);
  D_Flip_Flop #(.trigger("high")) d_ff_1 (.clk(in_3), .D(xor_1_out), .Q(SUM), .reset(rst));  // open: Qn, preset, en
  // AND_Gate and_2 has open pins: in0=and_1_out, in1=ha_1_out_4, out=open
  xor xor_2 (xor_2_out, and_1_out, ha_1_out_4);
  D_Flip_Flop #(.trigger("high")) d_ff_2 (
    .clk(in_3), .D(xor_2_out), .Q(d_ff_2_q), .reset(rst));  // open: Qn, preset, en

  // Notes on the sheet:
  //   FDHA
  //   HSUM1
  //   CAR1
  //   SC
endmodule

module main (
  input  in_1,
  input  in_2,
  input  in_3,
  input  in_4,
  input  x0,
  input  in_6,
  input  x1,
  input  x2,
  input  p3,
  input  p2,
  input  x3,
  input  p1,
  input  p0,
  input  x4,
  input  p7,
  input  x5,
  input  x6,
  input  x7,
  input  in_19
);

  wire and_1_out, and_2_out, and_3_out, and_4_out, and_5_out, and_6_out, and_7_out, and_8_out, and_9_out,
       clock_1_out, comparator_1_gt, comparator_2_eq, counter_2_carry, csadd_1_sum, csadd_2_sum, csadd_3_sum,
       csadd_4_sum, csadd_5_sum, csadd_6_sum, csadd_7_sum, not_1_out, shift_register_1_out,
       shift_register_2_q0, shift_register_2_q1, shift_register_2_q2, shift_register_2_q3, tcmp_1_out_4,
       undriven, undriven_2, undriven_3, unit_digit_1_g, unit_digit_2_a, unit_digit_2_b, unit_digit_2_c,
       unit_digit_2_d, unit_digit_2_e, unit_digit_2_f, unit_digit_2_g, unit_digit_3_a, unit_digit_3_b,
       unit_digit_3_c, unit_digit_3_d, unit_digit_3_e, unit_digit_3_f, unit_digit_3_g;
  wire [3:0] counter_1_q, counter_2_q;

  Shift_Register shift_register_1 (
    .clk(clock_1_out), .out(shift_register_1_out));  // open: shift, in, load, clr, d0, q0, d1, q1, d2, q2, d3, q3, d4, q4, d5, q5, d6, q6, d7, q7
  Clock clock_1 (.out(clock_1_out));
  Counter #(.width(4), .max('h8), .ongoal("stay")) counter_1 (
    .Q(counter_1_q), .clk(clock_1_out), .clr(undriven));  // open: load, D, count, carry
  Comparator #(.width(4)) comparator_1 (.a(counter_1_q), .b(4'b1111), .gt(comparator_1_gt));  // open: eq, lt
  and and_1 (and_1_out, x0, shift_register_1_out);
  and and_2 (and_2_out, x1, shift_register_1_out);
  and and_3 (and_3_out, x2, shift_register_1_out);
  and and_4 (and_4_out, x3, shift_register_1_out);
  and and_5 (and_5_out, x4, shift_register_1_out);
  and and_6 (and_6_out, x5, x5, shift_register_1_out);
  and and_7 (and_7_out, x6, shift_register_1_out);
  and and_8 (and_8_out, x7, shift_register_1_out);
  and and_9 (and_9_out, comparator_1_gt, clock_1_out);
  CSADD csadd_1 (.X(and_1_out), .Y(csadd_2_sum), .SUM(csadd_1_sum), .rst(in_19), .in_3(clock_1_out));
  CSADD csadd_2 (.X(and_2_out), .Y(csadd_3_sum), .SUM(csadd_2_sum), .rst(in_19), .in_3(clock_1_out));
  CSADD csadd_3 (.X(and_3_out), .Y(csadd_4_sum), .SUM(csadd_3_sum), .rst(in_19), .in_3(clock_1_out));
  CSADD csadd_4 (.X(and_4_out), .Y(csadd_5_sum), .SUM(csadd_4_sum), .rst(in_19), .in_3(clock_1_out));
  CSADD csadd_5 (.X(and_5_out), .Y(csadd_6_sum), .SUM(csadd_5_sum), .rst(in_19), .in_3(clock_1_out));
  CSADD csadd_6 (.X(and_6_out), .Y(csadd_7_sum), .SUM(csadd_6_sum), .rst(in_19), .in_3(clock_1_out));
  CSADD csadd_7 (.X(and_7_out), .Y(tcmp_1_out_4), .SUM(csadd_7_sum), .rst(in_19), .in_3(clock_1_out));
  TCMP tcmp_1 (.A(and_8_out), .reset(in_19), .out_4(tcmp_1_out_4), .clk(clock_1_out));
  not not_1 (not_1_out, comparator_2_eq);
  Comparator #(.width(4)) comparator_2 (.a(counter_2_q), .b(4'b1111), .eq(comparator_2_eq));  // open: gt, lt
  Counter #(.width(4), .max('hf), .ongoal("stay")) counter_2 (
    .Q(counter_2_q), .carry(counter_2_carry), .clk(clock_1_out), .clr(in_1));  // open: load, D, count
  Shift_Register #(.length(16)) shift_register_2 (
    .shift(not_1_out), .in(csadd_1_sum), .clk(clock_1_out), .q0(shift_register_2_q0),
    .q1(shift_register_2_q1), .q2(shift_register_2_q2), .q3(shift_register_2_q3));  // open: out, load, clr, d0, d1, d2, d3, d4, q4, d5, q5, d6, q6, d7, q7, d8, q8, d9, q9, d10, q10, d11, q11, d12, q12, d13, q13, d14, q14, d15, q15
  unit_digit unit_digit_1 (
    .p3(shift_register_2_q0), .p2(in_4), .p1(in_6), .p0(undriven_2), .g(unit_digit_1_g));  // open: a, b, c, d, e, f
  _7_Segment_Display u_7_segment_display_1 (.g(unit_digit_1_g));  // open: f, a, b, e, d, c, dp
  unit_digit unit_digit_2 (
    .p3(p3), .p2(p2), .p1(p1), .p0(p0), .a(unit_digit_2_a), .b(unit_digit_2_b), .c(unit_digit_2_c),
    .d(unit_digit_2_d), .e(unit_digit_2_e), .f(unit_digit_2_f), .g(unit_digit_2_g));
  _7_Segment_Display u_7_segment_display_2 (.g(p7));  // open: f, a, b, e, d, c, dp
  unit_digit unit_digit_3 (
    .p3(undriven_3), .p2(shift_register_2_q2), .p1(shift_register_2_q3), .p0(shift_register_2_q1),
    .a(unit_digit_3_a), .b(unit_digit_3_b), .c(unit_digit_3_c), .d(unit_digit_3_d), .e(unit_digit_3_e),
    .f(unit_digit_3_f), .g(unit_digit_3_g));
  _7_Segment_Display u_7_segment_display_3 (
    .g(unit_digit_2_g), .f(unit_digit_2_f), .a(unit_digit_2_a), .b(unit_digit_2_b), .e(unit_digit_2_e),
    .d(unit_digit_2_d), .c(unit_digit_2_c));  // open: dp
  _7_Segment_Display u_7_segment_display_4 (
    .g(unit_digit_3_g), .f(unit_digit_3_f), .a(unit_digit_3_a), .b(unit_digit_3_b), .e(unit_digit_3_e),
    .d(unit_digit_3_d), .c(unit_digit_3_c));  // open: dp

  // Notes on the sheet:
  //   y- serial in 
  //   reset
  //   clk
  //   serial output
endmodule

module TCMP (
  input  A,
  input  clk,
  input  reset,
  output out_4
);

  wire d_ff_2_q, FDHA_out, or_1_out, xor_1_out;

  and FDHA (FDHA_out, A, d_ff_2_q);
  xor xor_1 (xor_1_out, A, d_ff_2_q);
  D_Flip_Flop #(.trigger("high")) d_ff_1 (.clk(clk), .D(xor_1_out), .Q(out_4), .reset(reset));  // open: Qn, preset, en
  or or_1 (or_1_out, A, d_ff_2_q);
  D_Flip_Flop #(.trigger("high")) d_ff_2 (
    .clk(clk), .D(or_1_out), .Q(d_ff_2_q), .reset(reset));  // open: Qn, preset, en
endmodule

module unit_digit (
  input  p3,
  input  p2,
  input  p1,
  input  p0,
  output a,
  output b,
  output c,
  output d,
  output e,
  output f,
  output g
);

  wire and_1_out, and_2_out, and_3_out, and_4_out, and_5_out, and_6_out, and_7_out, and_8_out, and_9_out,
       and_10_out, and_11_out, and_12_out, and_13_out, and_14_out, and_15_out, and_16_out, not_1_out,
       not_2_out, not_3_out, not_4_out, not_5_out, not_6_out, not_7_out, not_8_out, not_9_out, not_10_out,
       not_11_out, not_12_out, not_13_out, not_14_out, not_15_out, not_16_out, not_17_out, not_18_out,
       not_19_out, not_20_out, not_21_out;

  not not_1 (not_1_out, p2);
  and and_1 (and_1_out, not_1_out, not_2_out);
  not not_2 (not_2_out, p0);
  and and_2 (and_2_out, p2, p0);
  not not_3 (not_3_out, p2);
  not not_4 (not_4_out, p1);
  and and_3 (and_3_out, not_4_out, not_5_out);
  not not_5 (not_5_out, p0);
  and and_4 (and_4_out, p1, p0);
  not not_6 (not_6_out, p1);
  or or_1 (c, not_6_out, p0, p2);
  not not_7 (not_7_out, p2);
  and and_5 (and_5_out, not_7_out, not_8_out);
  not not_8 (not_8_out, p0);
  not not_9 (not_9_out, p2);
  and and_6 (and_6_out, not_9_out, p1);
  and and_7 (and_7_out, p1, not_10_out);
  not not_10 (not_10_out, p0);
  not not_11 (not_11_out, p1);
  and and_8 (and_8_out, p2, not_11_out, p0);
  not not_12 (not_12_out, p2);
  and and_9 (and_9_out, not_12_out, not_13_out);
  not not_13 (not_13_out, p0);
  and and_10 (and_10_out, p1, not_14_out);
  not not_14 (not_14_out, p0);
  not not_15 (not_15_out, p1);
  and and_11 (and_11_out, not_15_out, not_16_out);
  not not_16 (not_16_out, p0);
  and and_12 (and_12_out, p2, not_17_out);
  not not_17 (not_17_out, p1);
  and and_13 (and_13_out, p2, not_18_out);
  not not_18 (not_18_out, p0);
  not not_19 (not_19_out, p2);
  and and_14 (and_14_out, not_19_out, p1);
  and and_15 (and_15_out, p2, not_20_out);
  not not_20 (not_20_out, p1);
  and and_16 (and_16_out, p2, not_21_out);
  not not_21 (not_21_out, p0);
  or or_2 (a, and_1_out, p1, and_2_out, p3);
  or or_3 (b, not_3_out, and_3_out, and_4_out);
  or or_4 (d, and_5_out, and_6_out, and_7_out, and_8_out, p3);
  or or_5 (e, and_9_out, and_10_out);
  or or_6 (f, and_11_out, and_12_out, and_13_out, p3);
  or or_7 (g, and_14_out, and_15_out, and_16_out, p3);
endmodule

module HA (
  input  in_1,
  input  in_2,
  output out_3,
  output out_4
);

  xor xor_1 (out_3, in_1, in_2);
  and and_1 (out_4, in_1, in_2);
endmodule

module mainn (
  input  X7,
  input  in_2,
  input  in_3,
  input  in_4,
  input  in_5,
  input  in_6,
  input  in_7,
  input  in_8,
  input  in_9,
  input  in_10
);

  wire and_1_out, and_2_out, and_3_out, and_4_out, and_5_out, and_6_out, and_7_out, and_8_out, and_9_out,
       clock_1_out, comparator_1_gt, counter_1_out_2, csa_1_sum, csa_2_sum, csa_3_sum, csa_4_sum, csa_5_sum,
       csa_6_sum, csa_7_sum, shift_register_1_out, shift_register_2_q0, tcmp_1_out_4, unit_digit_1_g;
  wire [3:0] counter_2_q;

  Shift_Register shift_register_1 (
    .clk(counter_1_out_2), .out(shift_register_1_out));  // open: shift, in, load, clr, d0, q0, d1, q1, d2, q2, d3, q3, d4, q4, d5, q5, d6, q6, d7, q7
  counter counter_1 (.clk(clock_1_out), .out_2(counter_1_out_2));
  Clock clock_1 (.out(clock_1_out));
  and and_1 (and_1_out, shift_register_1_out, X7);
  and and_2 (and_2_out, shift_register_1_out, in_2);
  TCMP tcmp_1 (.A(and_1_out), .out_4(tcmp_1_out_4), .clk(counter_1_out_2));  // open: reset
  CSA csa_1 (.x(and_2_out), .y(tcmp_1_out_4), .clr(in_9), .CLK(counter_1_out_2), .sum(csa_1_sum));
  and and_3 (and_3_out, shift_register_1_out, in_3);
  CSA csa_2 (.x(and_3_out), .y(csa_1_sum), .clr(in_9), .CLK(counter_1_out_2), .sum(csa_2_sum));
  and and_4 (and_4_out, shift_register_1_out, in_4);
  and and_5 (and_5_out, shift_register_1_out, in_5);
  CSA csa_3 (.x(and_4_out), .y(csa_2_sum), .clr(in_9), .CLK(counter_1_out_2), .sum(csa_3_sum));
  and and_6 (and_6_out, shift_register_1_out, in_6);
  CSA csa_4 (.x(and_5_out), .y(csa_3_sum), .clr(in_9), .CLK(counter_1_out_2), .sum(csa_4_sum));
  and and_7 (and_7_out, shift_register_1_out, in_7);
  CSA csa_5 (.x(and_7_out), .y(csa_6_sum), .clr(in_9), .CLK(counter_1_out_2), .sum(csa_5_sum));
  CSA csa_6 (.x(and_6_out), .y(csa_4_sum), .clr(in_9), .CLK(counter_1_out_2), .sum(csa_6_sum));
  buf and_8 (and_8_out, shift_register_1_out);  // AND_Gate
  CSA csa_7 (.x(and_8_out), .y(csa_5_sum), .clr(in_9), .CLK(counter_1_out_2), .sum(csa_7_sum));
  Counter #(.width(4), .max('hf)) counter_2 (.Q(counter_2_q), .clk(clock_1_out));  // open: load, D, count, carry, clr
  Shift_Register #(.length(16)) shift_register_2 (
    .in(csa_7_sum), .clk(and_9_out), .q0(shift_register_2_q0));  // open: shift, out, load, clr, d0, d1, q1, d2, q2, d3, q3, d4, q4, d5, q5, d6, q6, d7, q7, d8, q8, d9, q9, d10, q10, d11, q11, d12, q12, d13, q13, d14, q14, d15, q15
  Comparator #(.width(4)) comparator_1 (.a(counter_2_q), .b(4'b1111), .gt(comparator_1_gt));  // open: eq, lt
  and and_9 (and_9_out, comparator_1_gt, clock_1_out);
  unit_digit unit_digit_1 (
    .p3(shift_register_2_q0), .p2(in_10), .p1(in_10), .p0(in_10), .g(unit_digit_1_g));  // open: a, b, c, d, e, f
  _7_Segment_Display u_7_segment_display_1 (.g(unit_digit_1_g));  // open: f, a, b, e, d, c, dp

  // Notes on the sheet:
  //   Sign
endmodule

module CSA (
  input  x,
  input  y,
  input  clr,
  input  CLK,
  output sum
);

  wire d_ff_2_q, FDHA_2_out, FDHA_out, HA_out_3, HA_out_4, xor_1_out, xor_2_out;

  and FDHA (FDHA_out, HA_out_3, x);
  xor xor_1 (xor_1_out, x, HA_out_3);
  D_Flip_Flop d_ff_1 (.clk(CLK), .D(xor_1_out), .Q(sum), .reset(clr));  // open: Qn, preset, en
  HA HA (.in_1(y), .in_2(d_ff_2_q), .out_3(HA_out_3), .out_4(HA_out_4));
  xor xor_2 (xor_2_out, HA_out_4, FDHA_out);
  D_Flip_Flop d_ff_2 (.clk(CLK), .D(xor_2_out), .Q(d_ff_2_q), .reset(clr));  // open: Qn, preset, en
  and FDHA_2 (FDHA_2_out, FDHA_out, HA_out_4);

  // Notes on the sheet:
  //   sc
endmodule

module counter (
  input  clk,
  output out_2
);

  wire comparator_1_gt;
  wire [3:0] counter_1_q;

  Counter #(.width(4), .max('h8), .ongoal("stay")) counter_1 (
    .Q(counter_1_q), .clk(clk));  // open: load, D, count, carry, clr
  Comparator #(.width(4)) comparator_1 (.a(counter_1_q), .b(4'b1001), .gt(comparator_1_gt));  // open: eq, lt
  and and_1 (out_2, comparator_1_gt, clk);
endmodule
